# Fritzing sketch circuito_1 (saved by Fritzing 0.9.3b)
breadboards: 1

parts:
  Componente1 = FTDI Basic Programmer
  Componente4 = Arduino Nano (Rev3.0)
  FC-2 = Sound Sensor
  Mod2 = KY-013 Analog Temperature Sensor Module [package="Breakout board"]
  Mod3 = KY-026 Flame Sensor Module [package="Breakout board"]
  USBTTL1 = USB A Plug
  Raspberry_Pi_1 = Raspberry Pi 4 [part_number=RPI-4-b]  # not connected
  USBTTL2 = Micro USB B Plug  # not connected
  USBTTL3 = Micro USB B Plug
  USBTTL4 = USB A Plug  # not connected
  Componente5 = Bluetooth HC-05 Macho

nets:
  N1: Componente1.RXI, Componente5.TXD
  N2: Componente1.TXO, Componente5.RXD
  N3: Componente1.POWER, Componente5.VCC
  GND: Componente1.GND, Componente5.GND
  GND_2: Componente4.GND, FC-2.GND, Mod2.-, Mod3.G
  N4: Componente4.D2, Mod3.D0
  N5: Componente4.D3, FC-2.OUT
  5V: Componente4.5V, FC-2.VCC, Mod2.Vin, Mod3.+
  N6: Componente4.A7, Mod2.S
  N7: USBTTL1.usb, USBTTL3.usb

notes:
  CIRCUITO 1
  Autor: David Roni Hernández Beltrán

custom parts:
  FTDI Basic Programmer: Description: This is the newest revision of our FTDI Basic. We now use a SMD 6-pin header on the bottom, which makes it smaller and more compact. Functionality has remained the same. This is a basic breakout board for the FTDI FT232RL USB to serial IC. The pinout of this board matches the FTDI cable to work with official Arduino and cloned 3.3V Arduino boards. It can also be used for general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
  KY-013 Analog Temperature Sensor Module: KY-013 Analog Temperature Sensor module, measures ambient temperature based on resistance of the thermistor.
  KY-026 Flame Sensor Module: KY-026 Flame Sensor Module reacts in the presence of fire.
  USB A Plug: USB A Plug breadboard only for documetnation purposes.
  Raspberry Pi 4: The RPi4, a faster version of the awesome Raspberry Pi 2 B ARM Board with 40 pin gpio. Ready for special Raspberry Pi B+ and RPi2 Hat (Hardware attached (on) top)
